# Fritzing sketch Untitled Sketch 2 (saved by Fritzing 0.9.4)

parts:
  Компонент1 = Arduino Nano (Rev3.0)
  S1 = Round Pushbutton
  BAT1 = BC9VPC [package=bc9vpc]
  NEOPIXEL1 = Neopixel Strip -- White (60/m)
  R1 = Rotary Potentiometer (Small) [maximum_resistance=100kΩ package=THT]

nets:
  N1: Компонент1.D2, NEOPIXEL1.+5V
  N2: Компонент1.VIN, BAT1.V+
  GND: Компонент1.GND, BAT1.V-, NEOPIXEL1.GND, R1.leg2
  N3: Компонент1.5V, NEOPIXEL1.DI, R1.leg1
  N4: Компонент1.A2, S1.leg1
  N5: Компонент1.A1, R1.wiper
  N6: Компонент1.3V3, S1.leg0

custom parts:
  Neopixel Strip -- White (60/m): Neopixel Strip, White, 60 pixels per meter.

// code stored in the sketch: Untitled2.ino
i
